# Fritzing sketch Accelerometer (saved by Fritzing 0.3.16b)
breadboards: 1

parts:
  R1 = Resistor [resistance=10k package=THT]
  R2 = Resistor [resistance=10k package=THT]
  U1 = 3-Axis Accelerometer Breakout
  Arduino1 = Arduino
  IC1 = IC, SIP package, 8 pins [chip_label=ADXL345 spacing=300mil]  # not connected

nets:
  VDD: R1.Pin_0, R2.Pin_0, U1.VDD, Arduino1.3V3
  N1: R1.Pin_1, R2.Pin_1, U1.Y, U1.X, Arduino1.A4, Arduino1.A5
  GND: U1.GND, Arduino1.GND
